# Fritzing sketch ESP32-P4_Max31855_Thermocouple (saved by Fritzing 1.0.8)
circuit board: 8.46667cm x 5.64444cm
breadboards: 1

parts:
  Bauteil1 = Adafruit Thermocouple Amplifier MAX31855 [part_number="Adafruit #269"]
  Mod1 = Waveshare ESP32-P4-ETH [part_number=ESP32-P4-ETH]

nets:
  +3V3: Bauteil1.+3V3, Mod1.3V3
  N1: Bauteil1.GND, Mod1.GND_1, Mod1.GND_2, Mod1.GND_3, Mod1.GND_4, Mod1.GND_6, Mod1.GND_7, Mod1.GND_8, Mod1.GND_9
  N2: Bauteil1.DO, Mod1.GPIO19
  N3: Bauteil1.CS, Mod1.GPIO17
  N4: Bauteil1.CLK, Mod1.GPIO18

custom parts:
  Adafruit Thermocouple Amplifier MAX31855: Thermocouples are very sensitive, requiring a good amplifier with a cold-compensation reference. The MAX31855K does everything for you, and can be easily interfaced with any microcontroller, even one without an analog input. This breakout board has the chip itself, a 3.3V regulator with 10uF bypass capacitors and level shifting circuitry, all assembled and tested. Comes with a 2 pin terminal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
  Waveshare ESP32-P4-ETH: Waveshare ESP32-P4-ETH Board with 0.5 inch pin spacing to leave 2 free breadboard rows on each side.
